# Fritzing sketch solar_tracker_schematics (saved by Fritzing 0.9.5d)
breadboards: 1
perfboards: 1

parts:
  Part1 = Arduino Uno (Rev3)
  R1 = Resistor [tolerance=±5% resistance=10k package=THT]
  R2 = Resistor [tolerance=±5% resistance=10k package=THT]
  R3 = Photocell (LDR) [package=THT]
  R4 = Photocell (LDR) [package=THT]
  S1 = Toggle Switch [package=THT]
  J1 = Basic Servo
  J2 = male pin header, 6 pins [form="♂ (male)"]
  J3 = male pin header, 3 pins [form="♂ (male)"]
  R5 = Resistor [tolerance=±5% resistance=10k package=THT]
  R6 = Resistor [tolerance=±5% resistance=10k package=THT]
  R7 = Photocell (LDR) [package=THT]
  R8 = Photocell (LDR) [package=THT]
  S2 = Toggle Switch [package=THT]
  J4 = Basic Servo
  Part2 = Arduino Uno (Rev3)

nets:
  N1: Part1.A0, R1.Pin_1, R3.pin_0
  N2: Part1.A1, R2.Pin_1, R4.pin_0
  N3: Part1.A2, S1.COM
  N4: Part1.D3_PWM, J1.pulse
  5V: Part1.5V, R3.pin_1, S1.L1, J1.vcc
  GND: Part1.GND, R1.Pin_0, R2.Pin_0, S1.L2, J1.gnd
  N5: J2.pin1, S2.L2, Part2.5V
  N6: J2.pin2, Part2.GND
  N7: J2.pin3, Part2.D3_PWM
  N8: J2.pin4, S2.COM, Part2.A2
  N9: J2.pin5, R5.Pin_0, R8.pin_0, Part2.A1
  N10: J2.pin6, R6.Pin_1, R7.pin_1, Part2.A0
  N11: J3.pin3, J4.pulse
  N12: R5.Pin_1, J4.gnd
  N13: R6.Pin_0, S2.L1
  N14: R7.pin_0, R8.pin_1

notes:
  Breadboard
  Soldering Board
